# Fritzing sketch schematics (saved by Fritzing 0.9.3b)
circuit board: 8.46667cm x 5.64444cm
breadboards: 1
perfboards: 3

parts:
  Raspberry_Pi_1 = Raspberry Pi 3 [part_number=RPI-3-V1.2]
  LED1 = LED - 3mm [color="Red (633nm)" package="3 mm [THT]"]
  R1 = Resistor [tolerance=±5% resistance=150 package=THT]
  LED2 = LED - 3mm [color="Red (633nm)" package="3 mm [THT]"]
  R2 = Resistor [tolerance=±5% resistance=150 package=THT]
  LED3 = LED - 3mm [color="Red (633nm)" package="3 mm [THT]"]
  R3 = Resistor [tolerance=±5% resistance=150 package=THT]
  LED4 = LED - 3mm [color="Red (633nm)" package="3 mm [THT]"]
  R4 = Resistor [tolerance=±5% resistance=150 package=THT]
  R5 = Resistor [tolerance=±5% resistance=150 package=THT]
  R6 = Resistor [tolerance=±5% resistance=150 package=THT]
  LED5 = LED - 3mm [color="Red (633nm)" package="3 mm [THT]"]
  LED6 = LED - 3mm [color="Red (633nm)" package="3 mm [THT]"]
  LED7 = LED - 3mm [color="Red (633nm)" package="3 mm [THT]"]
  S1 = Pushbutton [package="[THT]"]
  R7 = Resistor [tolerance=±5% resistance=150 package=THT]
  S8 = Pushbutton [package="[THT]"]
  R8 = Resistor [tolerance=±5% resistance=150 package=THT]
  LED8 = LED - 3mm [color="Red (633nm)" package="3 mm [THT]"]
  S9 = Reed switch [package=THT]
  S10 = Reed switch [package=THT]
  S11 = Reed switch [package=THT]
  S12 = Reed switch [package=THT]  # not connected
  S13 = Reed switch [package=THT]
  S14 = Reed switch [package=THT]

nets:
  N1: Raspberry_Pi_1.GPIO3, S10.pin_1
  N2: Raspberry_Pi_1.GIPO4, S11.pin_1
  N3: Raspberry_Pi_1.GND, R1.Pin_1, R2.Pin_1, R3.Pin_1, R4.Pin_0, R5.Pin_0, R6.Pin_0, S1.Pin_1, S1.Pin_2, S8.Pin_3, S8.Pin_4, S9.pin_2, S10.pin_2, S11.pin_2, S13.pin_1, S14.pin_1
  N4: Raspberry_Pi_1.GIPO27, S13.pin_2
  N5: Raspberry_Pi_1.GIPO22, S14.pin_2
  N6: Raspberry_Pi_1.GIPO5, S8.Pin_1, S8.Pin_2, LED8.cathode
  N7: Raspberry_Pi_1.GIPO6, LED7.cathode, S1.Pin_3, S1.Pin_4
  N8: Raspberry_Pi_1.GIPO7, R8.Pin_0
  N9: Raspberry_Pi_1.GIPO8, R7.Pin_1
  N10: Raspberry_Pi_1.GIPO25, LED6.anode
  N11: Raspberry_Pi_1.GIPO24, LED5.anode
  N12: Raspberry_Pi_1.GIPO23, LED4.anode
  N13: Raspberry_Pi_1.GIPO18, LED3.anode
  N14: Raspberry_Pi_1.GIPO15, LED2.anode
  N15: Raspberry_Pi_1.GIPO14, LED1.anode
  N16: LED1.cathode, R1.Pin_0
  N17: LED2.cathode, R2.Pin_0
  N18: LED3.cathode, R3.Pin_0
  N19: LED4.cathode, R6.Pin_1
  N20: R4.Pin_1, LED5.cathode
  N21: R5.Pin_1, LED6.cathode
  N22: LED7.anode, R7.Pin_0
  N23: R8.Pin_1, LED8.anode
