# Fritzing sketch storegg (saved by Fritzing 0.9.3b)
perfboards: 2

parts:
  S17 = Reed switch [package=THT]
  S18 = Reed switch [package=THT]
  S19 = Reed switch [package=THT]
  S20 = Reed switch [package=THT]
  S22 = Reed switch [package=THT]
  LED25 = smd LED [color="Yellow (585nm)" package="0603 [SMD]"]
  S21 = Reed switch [package=THT]
  R3 = Resistor [tolerance=±5% resistance=220 package=THT]
  LED27 = smd LED [color="Red (633nm)" package="0603 [SMD]"]
  LED28 = smd LED [color="Red (633nm)" package="0603 [SMD]"]
  LED29 = smd LED [color="Red (633nm)" package="0603 [SMD]"]
  LED30 = smd LED [color="Green (565nm)" package="0603 [SMD]"]
  LED31 = smd LED [color="Green (565nm)" package="0603 [SMD]"]
  LED32 = smd LED [color="Yellow (585nm)" package="0603 [SMD]"]
  LED33 = smd LED [color="Yellow (585nm)" package="0603 [SMD]"]
  LED34 = smd LED [color="Yellow (585nm)" package="0603 [SMD]"]
  J2 = double row male pin header, 20 pins [form="♂ (male)"]
  J3 = double row male pin header, 20 pins [form="♂ (male)"]
  R13 = Resistor [tolerance=±5% resistance=220 package=THT]
  LED35 = smd LED [color="Yellow (585nm)" package="0603 [SMD]"]
  LED36 = smd LED [color="Yellow (585nm)" package="0603 [SMD]"]
  S23 = Toggle Switch [package=THT]
  S24 = Toggle Switch [package=THT]
  R14 = Resistor [tolerance=±5% resistance=220 package=THT]
  R15 = Resistor [tolerance=±5% resistance=220 package=THT]
  R16 = Resistor [tolerance=±5% resistance=220 package=THT]
  R17 = Resistor [tolerance=±5% resistance=220 package=THT]
  R18 = Resistor [tolerance=±5% resistance=220 package=THT]
  R19 = Resistor [tolerance=±5% resistance=220 package=THT]
  R20 = Resistor [tolerance=±5% resistance=220 package=THT]
  R21 = Resistor [tolerance=±5% resistance=220 package=THT]
  R22 = Resistor [tolerance=±5% resistance=220 package=THT]
  J5 = longpad pin header, 8 pins [form="long pad"]
  LED37 = smd LED [color="Yellow (585nm)" package="0603 [SMD]"]
  LED38 = smd LED [color="Yellow (585nm)" package="0603 [SMD]"]
  LED39 = smd LED [color="Yellow (585nm)" package="0603 [SMD]"]
  LED40 = smd LED [color="Yellow (585nm)" package="0603 [SMD]"]
  LED41 = smd LED [color="Yellow (585nm)" package="0603 [SMD]"]
  R23 = Resistor [tolerance=±5% resistance=220 package=THT]
  R25 = Resistor [tolerance=±5% resistance=220 package=THT]
  R26 = Resistor [tolerance=±5% resistance=220 package=THT]
  R27 = Resistor [tolerance=±5% resistance=220 package=THT]
  R28 = Resistor [tolerance=±5% resistance=220 package=THT]
  R29 = Resistor [tolerance=±5% resistance=220 package=THT]
  R30 = Resistor [tolerance=±5% resistance=220 package=THT]

nets:
  N1: S17.pin_1, LED25.anode
  N2: S18.pin_2, J2.pin2, J5.pin2, LED39.anode
  N3: S19.pin_1, J3.pin2, J5.pin5, LED40.anode
  N4: S20.pin_2, LED41.anode
  N5: S22.pin_1, S21.pin_2, J2.pin20, J5.pin1
  N6: S22.pin_2, LED38.anode
  N7: LED25.cathode, R26.Pin_1
  N8: S21.pin_1, LED37.anode
  N9: R3.Pin_1, LED37.cathode
  N10: LED27.cathode, R13.Pin_0
  N11: LED27.anode, J3.pin8
  N12: LED28.cathode, R14.Pin_0
  N13: LED28.anode, J3.pin9
  N14: LED29.cathode, R15.Pin_0
  N15: LED29.anode, J3.pin10
  N16: LED30.cathode, R17.Pin_0
  N17: LED30.anode, J3.pin12
  N18: LED31.cathode, R18.Pin_0
  N19: LED31.anode, J3.pin13
  N20: LED32.cathode, R22.Pin_0
  N21: LED32.anode, J3.pin17
  N22: LED33.cathode, R21.Pin_0
  N23: LED33.anode, J3.pin16
  N24: LED34.cathode, R20.Pin_0
  N25: LED34.anode, J3.pin15
  N26: J2.pin1, R22.Pin_1
  N27: J2.pin13, LED35.cathode, S23.L1, R30.Pin_0
  N28: J2.pin14, LED36.cathode, S24.L2, R29.Pin_0
  N29: J2.pin15, J5.pin7
  N30: J3.pin1, J5.pin6
  N31: J3.pin3, J5.pin4
  N32: J3.pin5, J5.pin3
  N33: LED35.anode, R16.Pin_0
  N34: LED36.anode, R19.Pin_0
  N35: J5.pin8, R23.Pin_1
  N36: LED38.cathode, R23.Pin_0
  N37: LED39.cathode, R28.Pin_1
  N38: LED40.cathode, R27.Pin_1
  N39: LED41.cathode, R25.Pin_1
